// Logisim project arcanoid.circ as structural Verilog: 10 circuits, main circuit main
module main (
);

  wire clock_1_out;
  wire [3:0] joystick_1_x;
  wire [4:0] control_bat_1_output_x_bat, video_scheme_1_chip_id_out, video_scheme_1_x_ball_out,
       video_scheme_1_x_bat_out, video_scheme_1_y_ball_out, video_scheme_2_chip_id_out,
       video_scheme_2_x_ball_out, video_scheme_2_x_bat_out, video_scheme_2_y_ball_out,
       video_scheme_3_chip_id_out, video_scheme_3_x_ball_out, video_scheme_3_x_bat_out,
       video_scheme_3_y_ball_out;
  wire [31:0] video_scheme_1_out_5, video_scheme_1_out_6, video_scheme_1_out_7, video_scheme_1_out_8,
       video_scheme_1_out_9, video_scheme_1_out_10, video_scheme_1_out_11, video_scheme_1_out_12,
       video_scheme_2_out_5, video_scheme_2_out_6, video_scheme_2_out_7, video_scheme_2_out_8,
       video_scheme_2_out_9, video_scheme_2_out_10, video_scheme_2_out_11, video_scheme_2_out_12,
       video_scheme_3_out_5, video_scheme_3_out_6, video_scheme_3_out_7, video_scheme_3_out_8,
       video_scheme_3_out_9, video_scheme_3_out_10, video_scheme_3_out_11, video_scheme_3_out_12,
       video_scheme_4_out_5, video_scheme_4_out_6, video_scheme_4_out_7, video_scheme_4_out_8,
       video_scheme_4_out_9, video_scheme_4_out_10, video_scheme_4_out_11, video_scheme_4_out_12;

  // Probe on joystick_1_x
  Joystick joystick_1 (.x(joystick_1_x));  // open: y
  Clock clock_1 (.out(clock_1_out));
  control_bat control_bat_1 (
    .x_bat(5'b10001), .gamepad_input(joystick_1_x), .clock(clock_1_out),
    .output_x_bat(control_bat_1_output_x_bat));
  // Probe on control_bat_1_output_x_bat
  DotMatrix #(.inputtype("row"), .matrixcols(32), .matrixrows(32)) dotmatrix_1 (
    .row0(video_scheme_1_out_9), .row1(video_scheme_1_out_5), .row2(video_scheme_1_out_10),
    .row3(video_scheme_1_out_6), .row4(video_scheme_1_out_11), .row5(video_scheme_1_out_7),
    .row6(video_scheme_1_out_12), .row7(video_scheme_1_out_8), .row8(video_scheme_2_out_9),
    .row9(video_scheme_2_out_5), .row10(video_scheme_2_out_10), .row11(video_scheme_2_out_6),
    .row12(video_scheme_2_out_11), .row13(video_scheme_2_out_7), .row14(video_scheme_2_out_12),
    .row15(video_scheme_2_out_8), .row16(video_scheme_3_out_9), .row17(video_scheme_3_out_5),
    .row18(video_scheme_3_out_10), .row19(video_scheme_3_out_6), .row20(video_scheme_3_out_11),
    .row21(video_scheme_3_out_7), .row22(video_scheme_3_out_12), .row23(video_scheme_3_out_8),
    .row24(video_scheme_4_out_9), .row25(video_scheme_4_out_5), .row26(video_scheme_4_out_10),
    .row27(video_scheme_4_out_6), .row28(video_scheme_4_out_11), .row29(video_scheme_4_out_7),
    .row30(video_scheme_4_out_12), .row31(video_scheme_4_out_8));
  video_scheme video_scheme_1 (
    .chip_ID({5{1'b0}}), .x_ball(5'b10000), .y_ball(5'b11100), .x_bat(control_bat_1_output_x_bat),
    .chip_ID_out(video_scheme_1_chip_id_out), .x_ball_out(video_scheme_1_x_ball_out),
    .y_ball_out(video_scheme_1_y_ball_out), .x_bat_out(video_scheme_1_x_bat_out),
    .out_9(video_scheme_1_out_9), .out_5(video_scheme_1_out_5), .out_10(video_scheme_1_out_10),
    .out_6(video_scheme_1_out_6), .out_11(video_scheme_1_out_11), .out_7(video_scheme_1_out_7),
    .out_12(video_scheme_1_out_12), .out_8(video_scheme_1_out_8));
  video_scheme video_scheme_2 (
    .chip_ID(video_scheme_1_chip_id_out), .x_ball(video_scheme_1_x_ball_out),
    .y_ball(video_scheme_1_y_ball_out), .x_bat(video_scheme_1_x_bat_out),
    .chip_ID_out(video_scheme_2_chip_id_out), .x_ball_out(video_scheme_2_x_ball_out),
    .y_ball_out(video_scheme_2_y_ball_out), .x_bat_out(video_scheme_2_x_bat_out),
    .out_9(video_scheme_2_out_9), .out_5(video_scheme_2_out_5), .out_10(video_scheme_2_out_10),
    .out_6(video_scheme_2_out_6), .out_11(video_scheme_2_out_11), .out_7(video_scheme_2_out_7),
    .out_12(video_scheme_2_out_12), .out_8(video_scheme_2_out_8));
  video_scheme video_scheme_3 (
    .chip_ID(video_scheme_2_chip_id_out), .x_ball(video_scheme_2_x_ball_out),
    .y_ball(video_scheme_2_y_ball_out), .x_bat(video_scheme_2_x_bat_out),
    .chip_ID_out(video_scheme_3_chip_id_out), .x_ball_out(video_scheme_3_x_ball_out),
    .y_ball_out(video_scheme_3_y_ball_out), .x_bat_out(video_scheme_3_x_bat_out),
    .out_9(video_scheme_3_out_9), .out_5(video_scheme_3_out_5), .out_10(video_scheme_3_out_10),
    .out_6(video_scheme_3_out_6), .out_11(video_scheme_3_out_11), .out_7(video_scheme_3_out_7),
    .out_12(video_scheme_3_out_12), .out_8(video_scheme_3_out_8));
  video_scheme video_scheme_4 (
    .chip_ID(video_scheme_3_chip_id_out), .x_ball(video_scheme_3_x_ball_out),
    .y_ball(video_scheme_3_y_ball_out), .x_bat(video_scheme_3_x_bat_out), .out_9(video_scheme_4_out_9),
    .out_5(video_scheme_4_out_5), .out_10(video_scheme_4_out_10), .out_6(video_scheme_4_out_6),
    .out_11(video_scheme_4_out_11), .out_7(video_scheme_4_out_7), .out_12(video_scheme_4_out_12),
    .out_8(video_scheme_4_out_8));  // open: chip_ID_out, x_ball_out, y_ball_out, x_bat_out
endmodule

// X
module contoler (
  input  up,
  input  down,
  input  clock,
  input  left,
  input  right,
  input  [4:0] x_bat,
  input  clock_2,
  output [4:0] X,
  output [4:0] X_2,
  output [4:0] output_x_bat
);

  wire comparator_1_eq, comparator_1_lt, comparator_2_eq, comparator_3_eq, not_1_out, not_2_out, or_1_out,
       or_2_out, or_3_out, or_4_out, or_5_out, or_6_out;
  wire [1:0] register_1_q, register_2_q;
  wire [3:0] undriven;
  wire [4:0] counter_3_q, multiplexer_1_out;

  or or_1 (or_1_out, up, down);
  or or_2 (or_2_out, left, right);
  Register #(.width(2)) register_1 (.D({down, up}), .Q(register_1_q), .clk(or_1_out), .clr(or_2_out));  // open: en
  Register #(.width(2)) register_2 (.D({right, left}), .Q(register_2_q), .clk(or_2_out), .clr(or_1_out));  // open: en
  or or_3 (or_3_out, not_2_out, comparator_3_eq);
  Comparator #(.width(4), .mode("unsigned")) comparator_1 (
    .a(undriven), .b(4'b1000), .eq(comparator_1_eq), .lt(comparator_1_lt));  // open: gt
  not not_1 (not_1_out, comparator_1_eq);
  Multiplexer #(.width(5)) multiplexer_1 (
    .in0(5'b01110), .in1(5'b10001), .out(multiplexer_1_out), .sel(or_3_out));  // open: en
  Counter #(.width(5), .max('h1f)) counter_1 (
    .load(register_1_q[1]), .count(or_4_out), .Q(X), .clk(clock));  // open: D, carry, clr
  or or_4 (or_4_out, register_1_q[0], register_1_q[1]);
  Counter #(.width(5), .max('h14)) counter_2 (
    .load(register_2_q[1]), .count(or_5_out), .Q(X_2), .clk(clock));  // open: D, carry, clr
  or or_5 (or_5_out, register_2_q[0], register_2_q[1]);
  Counter #(.width(5), .max('h1f)) counter_3 (
    .load(comparator_1_lt), .D(multiplexer_1_out), .count(not_1_out), .Q(counter_3_q), .clk(clock_2),
    .clr(or_6_out));  // open: carry
  or or_6 (or_6_out, comparator_3_eq, comparator_2_eq);
  Adder #(.width(5)) adder_1 (.a(x_bat), .b(counter_3_q), .out(output_x_bat));  // open: cin, cout
  Comparator #(.width(5), .mode("unsigned")) comparator_2 (
    .a(output_x_bat), .b({5{1'b1}}), .eq(comparator_2_eq));  // open: gt, lt
  Comparator #(.width(5), .mode("unsigned")) comparator_3 (
    .a(output_x_bat), .b(5'b00010), .eq(comparator_3_eq));  // open: gt, lt
  not not_2 (not_2_out, comparator_2_eq);
endmodule

// 0x1f
module control_bat (
  input  [4:0] x_bat,
  input  [3:0] gamepad_input,
  input  clock,
  output [4:0] output_x_bat
);

  wire and_1_out, and_2_out, comparator_1_eq, comparator_1_lt, comparator_2_eq, comparator_3_eq, not_1_out,
       not_2_out, not_3_out, not_4_out, or_1_out;
  wire [4:0] counter_1_q;

  not not_1 (not_1_out, comparator_1_eq);
  not not_2 (not_2_out, comparator_1_lt);
  and and_1 (and_1_out, comparator_3_eq, not_3_out, comparator_1_lt);
  not not_3 (not_3_out, comparator_1_eq);
  and and_2 (and_2_out, comparator_2_eq, not_1_out, not_2_out);
  Comparator #(.width(4), .mode("unsigned")) comparator_1 (
    .a(gamepad_input), .b(4'b1000), .eq(comparator_1_eq), .lt(comparator_1_lt));  // open: gt
  Counter #(.width(5), .max('h1f)) counter_1 (
    .load(comparator_1_lt), .D(5'b10001), .count(not_4_out), .Q(counter_1_q), .clk(clock));  // open: carry, clr
  not not_4 (not_4_out, or_1_out);
  or or_1 (or_1_out, comparator_1_eq, and_1_out, and_2_out);
  Adder #(.width(5)) adder_1 (.a(x_bat), .b(counter_1_q), .out(output_x_bat));  // open: cin, cout
  Comparator #(.width(5), .mode("unsigned")) comparator_2 (
    .a(output_x_bat), .b({5{1'b1}}), .eq(comparator_2_eq));  // open: gt, lt
  Comparator #(.width(5), .mode("unsigned")) comparator_3 (
    .a(output_x_bat), .b(5'b00010), .eq(comparator_3_eq));  // open: gt, lt
endmodule

module video_chip (
  input  [4:0] chip_ID,
  input  [4:0] x_ball,
  input  [4:0] y_ball,
  input  [4:0] x_bat,
  output [4:0] chip_ID_out,
  output [31:0] out,
  output [4:0] x_ball_out,
  output [4:0] y_ball_out,
  output [4:0] y_bat_out
);

  wire [31:0] decoder_32_inv_1_out, decoder_32_inv_2_out, shifter_1_out, shifter_2_out;

  Adder #(.width(5)) adder_1 (.a(5'b00001), .b(chip_ID), .out(chip_ID_out));  // open: cin, cout
  decoder_32_inv decoder_32_inv_1 (.data(x_ball), .A(y_ball), .B(chip_ID), .out(decoder_32_inv_1_out));
  decoder_32_inv decoder_32_inv_2 (.data(x_bat), .A(chip_ID), .B(5'b11101), .out(decoder_32_inv_2_out));
  Shifter #(.width(32)) shifter_1 (.in(decoder_32_inv_2_out), .\dist (5'b00010), .out(shifter_1_out));
  Shifter #(.width(32)) shifter_2 (.in(decoder_32_inv_2_out), .\dist (5'b00001), .out(shifter_2_out));
  assign out = decoder_32_inv_1_out | decoder_32_inv_2_out | shifter_1_out | shifter_2_out;  // OR_Gate or_1, 32 bits wide

  assign x_ball_out = x_ball;
  assign y_ball_out = y_ball;
  assign y_bat_out = x_bat;
endmodule

module inrange (
  input  [4:0] xball,
  input  [4:0] xbat,
  output shareArow
);

  wire comparator_1_eq, comparator_2_eq, comparator_3_eq;
  wire [4:0] adder_1_out, adder_2_out;

  Comparator #(.width(5)) comparator_1 (.a(xball), .b(xbat), .eq(comparator_1_eq));  // open: gt, lt
  Adder #(.width(5)) adder_1 (.a(xbat), .b(5'b00001), .out(adder_1_out));  // open: cin, cout
  Comparator #(.width(5)) comparator_2 (.a(xball), .b(adder_2_out), .eq(comparator_2_eq));  // open: gt, lt
  Adder #(.width(5)) adder_2 (.a(xbat), .b(5'b00010), .out(adder_2_out));  // open: cin, cout
  Comparator #(.width(5)) comparator_3 (.a(xball), .b(adder_1_out), .eq(comparator_3_eq));  // open: gt, lt
  or or_1 (shareArow, comparator_1_eq, comparator_3_eq, comparator_2_eq);
endmodule

module reflect (
  input  [2:0] oldv,
  output [2:0] newv
);

  wire comparator_1_eq;

  Comparator #(.width(3)) comparator_1 (.a(oldv), .b(3'b100), .eq(comparator_1_eq));  // open: gt, lt
endmodule

module kinematic_controller (
  input  clock,
  input  reset,
  input  [4:0] x_joystick,
  output [4:0] zero,
  output [4:0] ballx,
  output [4:0] bally,
  output [4:0] x_joystick_out,
  output [7:0] scoreA,
  output [15:0] bx,
  output [15:0] vx,
  output [15:0] by,
  output [15:0] vy
);


  assign x_joystick_out = x_joystick;
  assign zero = {5{1'b0}};

  // Other names for the same wires on the sheet: clk = clock; leftYout[4:0] = x_joystick; longVX[15:0] = vx;
  //   longVY[15:0] = vy; scA[7:0] = scoreA; xreg[15:0] = bx; yreg[15:0] = by
endmodule

module decoder_32 (
  input  [4:0] data,
  input  [4:0] A,
  input  [4:0] B,
  output [31:0] out
);

  wire comparator_1_eq;

  Comparator #(.width(5)) comparator_1 (.a(A), .b(B), .eq(comparator_1_eq));  // open: gt, lt
  Decoder #(.select(5), .disabled(0)) decoder_1 (
    .out0(out[0]), .out1(out[1]), .out2(out[2]), .out3(out[3]), .out4(out[4]), .out5(out[5]), .out6(out[6]),
    .out7(out[7]), .out8(out[8]), .out9(out[9]), .out10(out[10]), .out11(out[11]), .out12(out[12]),
    .out13(out[13]), .out14(out[14]), .out15(out[15]), .out16(out[16]), .out17(out[17]), .out18(out[18]),
    .out19(out[19]), .out20(out[20]), .out21(out[21]), .out22(out[22]), .out23(out[23]), .out24(out[24]),
    .out25(out[25]), .out26(out[26]), .out27(out[27]), .out28(out[28]), .out29(out[29]), .out30(out[30]),
    .out31(out[31]), .sel(data), .en(comparator_1_eq));
endmodule

module decoder_32_inv (
  input  [4:0] data,
  input  [4:0] A,
  input  [4:0] B,
  output [31:0] out
);

  wire comparator_1_eq;

  Comparator #(.width(5)) comparator_1 (.a(A), .b(B), .eq(comparator_1_eq));  // open: gt, lt
  Decoder #(.select(5), .disabled(0)) decoder_1 (
    .out0(out[31]), .out1(out[30]), .out2(out[29]), .out3(out[28]), .out4(out[27]), .out5(out[26]),
    .out6(out[25]), .out7(out[24]), .out8(out[23]), .out9(out[22]), .out10(out[21]), .out11(out[20]),
    .out12(out[19]), .out13(out[18]), .out14(out[17]), .out15(out[16]), .out16(out[15]), .out17(out[14]),
    .out18(out[13]), .out19(out[12]), .out20(out[11]), .out21(out[10]), .out22(out[9]), .out23(out[8]),
    .out24(out[7]), .out25(out[6]), .out26(out[5]), .out27(out[4]), .out28(out[3]), .out29(out[2]),
    .out30(out[1]), .out31(out[0]), .sel(data), .en(comparator_1_eq));
endmodule

module video_scheme (
  input  [4:0] chip_ID,
  input  [4:0] x_ball,
  input  [4:0] y_ball,
  input  [4:0] x_bat,
  output [31:0] out_5,
  output [31:0] out_6,
  output [31:0] out_7,
  output [31:0] out_8,
  output [31:0] out_9,
  output [31:0] out_10,
  output [31:0] out_11,
  output [31:0] out_12,
  output [4:0] chip_ID_out,
  output [4:0] x_ball_out,
  output [4:0] y_ball_out,
  output [4:0] x_bat_out
);

  wire [4:0] video_chip_1_chip_id_out, video_chip_1_x_ball_out, video_chip_1_y_ball_out,
       video_chip_1_y_bat_out, video_chip_2_chip_id_out, video_chip_2_x_ball_out, video_chip_2_y_ball_out,
       video_chip_2_y_bat_out, video_chip_3_chip_id_out, video_chip_3_x_ball_out, video_chip_3_y_ball_out,
       video_chip_3_y_bat_out, video_chip_4_chip_id_out, video_chip_4_x_ball_out, video_chip_4_y_ball_out,
       video_chip_4_y_bat_out, video_chip_5_chip_id_out, video_chip_5_x_ball_out, video_chip_5_y_ball_out,
       video_chip_5_y_bat_out, video_chip_6_chip_id_out, video_chip_6_x_ball_out, video_chip_6_y_ball_out,
       video_chip_6_y_bat_out, video_chip_7_chip_id_out, video_chip_7_x_ball_out, video_chip_7_y_ball_out,
       video_chip_7_y_bat_out;

  video_chip video_chip_1 (
    .chip_ID(chip_ID), .x_ball(x_ball), .y_ball(y_ball), .x_bat(x_bat),
    .chip_ID_out(video_chip_1_chip_id_out), .out(out_9), .x_ball_out(video_chip_1_x_ball_out),
    .y_ball_out(video_chip_1_y_ball_out), .y_bat_out(video_chip_1_y_bat_out));
  video_chip video_chip_2 (
    .chip_ID(video_chip_1_chip_id_out), .x_ball(video_chip_1_x_ball_out), .y_ball(video_chip_1_y_ball_out),
    .x_bat(video_chip_1_y_bat_out), .chip_ID_out(video_chip_2_chip_id_out), .out(out_5),
    .x_ball_out(video_chip_2_x_ball_out), .y_ball_out(video_chip_2_y_ball_out),
    .y_bat_out(video_chip_2_y_bat_out));
  video_chip video_chip_3 (
    .chip_ID(video_chip_2_chip_id_out), .x_ball(video_chip_2_x_ball_out), .y_ball(video_chip_2_y_ball_out),
    .x_bat(video_chip_2_y_bat_out), .chip_ID_out(video_chip_3_chip_id_out), .out(out_10),
    .x_ball_out(video_chip_3_x_ball_out), .y_ball_out(video_chip_3_y_ball_out),
    .y_bat_out(video_chip_3_y_bat_out));
  video_chip video_chip_4 (
    .chip_ID(video_chip_3_chip_id_out), .x_ball(video_chip_3_x_ball_out), .y_ball(video_chip_3_y_ball_out),
    .x_bat(video_chip_3_y_bat_out), .chip_ID_out(video_chip_4_chip_id_out), .out(out_6),
    .x_ball_out(video_chip_4_x_ball_out), .y_ball_out(video_chip_4_y_ball_out),
    .y_bat_out(video_chip_4_y_bat_out));
  video_chip video_chip_5 (
    .chip_ID(video_chip_4_chip_id_out), .x_ball(video_chip_4_x_ball_out), .y_ball(video_chip_4_y_ball_out),
    .x_bat(video_chip_4_y_bat_out), .chip_ID_out(video_chip_5_chip_id_out), .out(out_11),
    .x_ball_out(video_chip_5_x_ball_out), .y_ball_out(video_chip_5_y_ball_out),
    .y_bat_out(video_chip_5_y_bat_out));
  video_chip video_chip_6 (
    .chip_ID(video_chip_5_chip_id_out), .x_ball(video_chip_5_x_ball_out), .y_ball(video_chip_5_y_ball_out),
    .x_bat(video_chip_5_y_bat_out), .chip_ID_out(video_chip_6_chip_id_out), .out(out_7),
    .x_ball_out(video_chip_6_x_ball_out), .y_ball_out(video_chip_6_y_ball_out),
    .y_bat_out(video_chip_6_y_bat_out));
  video_chip video_chip_7 (
    .chip_ID(video_chip_6_chip_id_out), .x_ball(video_chip_6_x_ball_out), .y_ball(video_chip_6_y_ball_out),
    .x_bat(video_chip_6_y_bat_out), .chip_ID_out(video_chip_7_chip_id_out), .out(out_12),
    .x_ball_out(video_chip_7_x_ball_out), .y_ball_out(video_chip_7_y_ball_out),
    .y_bat_out(video_chip_7_y_bat_out));
  video_chip video_chip_8 (
    .chip_ID(video_chip_7_chip_id_out), .x_ball(video_chip_7_x_ball_out), .y_ball(video_chip_7_y_ball_out),
    .x_bat(video_chip_7_y_bat_out), .chip_ID_out(chip_ID_out), .out(out_8), .x_ball_out(x_ball_out),
    .y_ball_out(y_ball_out), .y_bat_out(x_bat_out));
endmodule
